// Logisim project mips.circ as structural Verilog: 15 circuits, main circuit MIPS
// pc_calc
module MIPS (
  input  in_1
);

  wire alu_1_alueq, and_1_out, and_3_out, control_1_alusrc, control_1_branch, control_1_extop,
       control_1_jump, control_1_mem2reg, control_1_memwr, control_1_noinst, control_1_regdst,
       control_1_regwr, d_ff_1_q, d_ff_1_qn, decoder_1_out0, decoder_1_out1, decoder_1_out2, decoder_1_out3,
       demultiplexer_1_out0, nor_1_out, nor_2_out, nor_3_out, not_1_out, not_2_out, not_3_out, not_4_out,
       or_1_out, undriven, undriven_2, undriven_3;
  wire [1:0] controlled_buffer_1_out_2;
  wire [4:0] instruction_splitter_1_rd, instruction_splitter_1_rs, instruction_splitter_1_rt,
       instruction_splitter_1_shamt, multiplexer_1_out;
  wire [5:0] control_1_aluctr, instruction_splitter_1_funct, instruction_splitter_1_opcode;
  wire [6:0] keyboard_1_data, multiplexer_3_out, ram_1_data_2, undriven_4;
  wire [8:7] Clock_out;
  wire [10:8] demultiplexer_1_out1;
  wire [15:0] instruction_splitter_1_immediate;
  wire [24:0] ram_1_data;
  wire [25:0] instruction_splitter_1_address;
  wire [31:0] alu_1_aluout, controlled_buffer_1_out, extender_1_output, Instruction_q, multiplexer_2_out,
       multiplexer_4_out, PC_2_q, pc_calc_w_delay_1_nextpc, register_file_1_busa, register_file_1_busb,
       register_file_1_t1, register_file_1_t2, register_file_1_t3;

  not not_1 (not_1_out, Clock_out[7]);
  Clock Clock (.out(Clock_out[7]));
  Button Reset (.out(demultiplexer_1_out1[8]));
  // Probe on pc_calc_w_delay_1_nextpc
  PC_Calc_w__Delay pc_calc_w_delay_1 (
    .Last_PC(PC_2_q), .extimm(extender_1_output), .address(instruction_splitter_1_address),
    .Rrs(register_file_1_busa), .jump(control_1_jump), .branch(control_1_branch), .Clk(Clock_out[7]),
    .Clr(demultiplexer_1_out1[8]), .nextpc(pc_calc_w_delay_1_nextpc));
  // Probe on PC_2_q
  Register #(.width(32)) PC_2 (
    .D(pc_calc_w_delay_1_nextpc), .Q(PC_2_q), .clk(Clock_out[7]), .clr(demultiplexer_1_out1[8]));  // open: en
  assign {controlled_buffer_1_out[31:16], controlled_buffer_1_out_2, controlled_buffer_1_out[13:0]} = Clock_out[7] ? PC_2_q : 32'bz;  // Controlled_Buffer controlled_buffer_1
  LED BUS (.in(nor_1_out));
  nor nor_1 (nor_1_out, nor_2_out, nor_3_out);
  D_Flip_Flop d_ff_1 (
    .clk(Clock_out[7]), .D(nor_1_out), .Q(d_ff_1_q), .Qn(d_ff_1_qn), .preset(d_ff_1_q), .en(in_1));  // open: reset
  Decoder #(.select(2), .enable("false")) decoder_1 (
    .out0(decoder_1_out0), .out1(decoder_1_out1), .out2(decoder_1_out2), .out3(decoder_1_out3),
    .sel(controlled_buffer_1_out_2));
  Register #(.width(32)) Instruction (
    .D({ram_1_data, ram_1_data_2}), .Q(Instruction_q), .clk(not_1_out), .clr(demultiplexer_1_out1[8]));  // open: en
  nor nor_2 (nor_2_out, controlled_buffer_1_out[0], controlled_buffer_1_out[1]);
  nor nor_3 (nor_3_out, or_1_out, and_1_out);
  // Probe on Instruction_q
  LED Clock_2 (.in(Clock_out[7]));
  // Probe on instruction_splitter_1_rs
  // Probe on instruction_splitter_1_rt
  // Probe on instruction_splitter_1_rd
  // Probe on multiplexer_1_out
  or or_1 (or_1_out, Clock_out[7], control_1_mem2reg);
  and and_1 (and_1_out, control_1_memwr, not_1_out);
  // Probe on multiplexer_4_out
  // Probe on instruction_splitter_1_opcode
  // Probe on instruction_splitter_1_funct
  Instruction_Splitter instruction_splitter_1 (
    .instruction(Instruction_q), .opcode(instruction_splitter_1_opcode), .rs(instruction_splitter_1_rs),
    .rt(instruction_splitter_1_rt), .rd(instruction_splitter_1_rd), .shamt(instruction_splitter_1_shamt),
    .funct(instruction_splitter_1_funct), .immediate(instruction_splitter_1_immediate),
    .address(instruction_splitter_1_address));
  // Probe on instruction_splitter_1_shamt
  // Probe on instruction_splitter_1_address
  // Probe on extender_1_output
  not not_2 (not_2_out, and_1_out);
  not not_3 (not_3_out, and_1_out);
  not not_4 (not_4_out, and_1_out);
  Demultiplexer #(.select(4), .enable("false")) demultiplexer_1 (
    .out0(demultiplexer_1_out0), .out1(demultiplexer_1_out1[9]), .in(decoder_1_out3),
    .sel(controlled_buffer_1_out[13:10]));  // open: out2, out3, out4, out5, out6, out7, out8, out9, out10, out11, out12, out13, out14, out15
  RAM #(.addrWidth(12), .dataWidth(32)) ram_1 (
    .addr(controlled_buffer_1_out[13:2]), .data({ram_1_data, ram_1_data_2}), .sel(decoder_1_out0),
    .clk(Clock_out[7]), .ld(not_2_out), .clr(undriven));
  RAM #(.addrWidth(12), .dataWidth(32)) ram_2 (
    .addr(controlled_buffer_1_out[13:2]), .data({ram_1_data, ram_1_data_2}), .sel(decoder_1_out1),
    .clk(Clock_out[7]), .ld(not_3_out), .clr(undriven_2));
  RAM #(.addrWidth(12), .dataWidth(32)) ram_3 (
    .addr(controlled_buffer_1_out[13:2]), .data({ram_1_data, ram_1_data_2}), .sel(decoder_1_out2),
    .clk(Clock_out[7]), .ld(not_4_out), .clr(undriven_3));
  // Probe on register_file_1_t1
  // Probe on register_file_1_t2
  // Probe on register_file_1_t3
  Register_File register_file_1 (
    .Ra(instruction_splitter_1_rs), .Rb(instruction_splitter_1_rt), .RegWr(control_1_regwr),
    .Rw(multiplexer_1_out), .busW(multiplexer_4_out), .t1(register_file_1_t1), .t2(register_file_1_t2),
    .t3(register_file_1_t3), .clk(Clock_out[7]), .clr(demultiplexer_1_out1[8]), .BusA(register_file_1_busa),
    .BusB(register_file_1_busb));
  Multiplexer #(.width(5), .enable("false")) multiplexer_1 (
    .in0(instruction_splitter_1_rt), .in1(instruction_splitter_1_rd), .out(multiplexer_1_out),
    .sel(control_1_regdst));
  Extender extender_1 (.Input(instruction_splitter_1_immediate), .Sign(control_1_extop), .Output(extender_1_output));
  // Probe on {controlled_buffer_1_out[31:16], controlled_buffer_1_out_2, controlled_buffer_1_out[13:0]}
  // Probe on {ram_1_data, ram_1_data_2}
  // Probe on register_file_1_busa
  // Probe on register_file_1_busb
  LED NOOP (.in(control_1_noinst));
  Control control_1 (
    .opcode(instruction_splitter_1_opcode), .funct(instruction_splitter_1_funct),
    .shamt(instruction_splitter_1_shamt), .zero(alu_1_alueq), .NoInst(control_1_noinst),
    .RegDst(control_1_regdst), .RegWr(control_1_regwr), .ExtOp(control_1_extop), .MemWr(control_1_memwr),
    .Mem2Reg(control_1_mem2reg), .ALUsrc(control_1_alusrc), .branch(control_1_branch), .jump(control_1_jump),
    .ALUctr(control_1_aluctr));
  assign {ram_1_data, ram_1_data_2} = demultiplexer_1_out1[9] ? {{25{1'b0}}, multiplexer_3_out} : 32'bz;  // Controlled_Buffer controlled_buffer_2
  // Probe on multiplexer_2_out
  Multiplexer #(.width(32), .enable("false")) multiplexer_2 (
    .in0(register_file_1_busb), .in1(extender_1_output), .out(multiplexer_2_out), .sel(control_1_alusrc));
  and and_2 (demultiplexer_1_out1[10], Clock_out[7], demultiplexer_1_out1[9], controlled_buffer_1_out[2]);
  Multiplexer #(.width(7), .enable("false")) multiplexer_3 (
    .in0(undriven_4), .in1(keyboard_1_data), .out(multiplexer_3_out), .sel(controlled_buffer_1_out[2]));
  // Probe on multiplexer_4_out
  // Probe on alu_1_aluout
  ALU alu_1 (
    .BusA(register_file_1_busa), .BusB(multiplexer_2_out), .ALUeq(alu_1_alueq), .ALUctr(control_1_aluctr),
    .ALUout(alu_1_aluout));
  // Probe on control_1_aluctr
  and and_3 (and_3_out, control_1_memwr, not_1_out);
  // Probe on keyboard_1_data
  assign {ram_1_data, ram_1_data_2} = and_3_out ? register_file_1_busb : 32'bz;  // Controlled_Buffer controlled_buffer_3
  assign {controlled_buffer_1_out[31:16], controlled_buffer_1_out_2, controlled_buffer_1_out[13:0]} = not_1_out ? alu_1_aluout : 32'bz;  // Controlled_Buffer controlled_buffer_4
  Control2 control2_1 ();  // open: opcode, funct, Branch, Jump, RegDst, RegWr, ExtOp, MemWr, Mem2Reg, ALUsrc
  Multiplexer #(.width(32), .enable("false")) multiplexer_4 (
    .in0(alu_1_aluout), .in1({ram_1_data, ram_1_data_2}), .out(multiplexer_4_out), .sel(control_1_mem2reg));
  and and_4 (Clock_out[8], demultiplexer_1_out0, and_1_out);
  TTY tty_1 (.data(ram_1_data_2), .clk(Clock_out[7]), .we(Clock_out[8]), .clr(demultiplexer_1_out1[8]));
  Keyboard keyboard_1 (
    .clk(demultiplexer_1_out1[10]), .re(demultiplexer_1_out1[9]), .clr(demultiplexer_1_out1[8]),
    .avail(undriven_4[0]), .data(keyboard_1_data));

  // Notes on the sheet:
  //   Clock
  //   !Clock
  //   Reset
  //   Data
  //   Address
  //   RegDst
  //   I/O sub-address
  //   ExtOp
  //   Byte Addr 0
  //   ALUSrc
  //   Byte Addr 0x4000
  //   Byte Addr 0x8000
  //   I/O
  //   Byte Addr 0xC000
  //   Mem2Reg
  //   BusA
  //   BusB
  //   Clock
  //   !Clock
  //   Reset
  //   Data
  //   Address
endmodule

// instr split
module Instruction_Splitter (
  input  [31:0] instruction,
  output [5:0] opcode,
  output [4:0] rs,
  output [4:0] rt,
  output [4:0] rd,
  output [4:0] shamt,
  output [5:0] funct,
  output [15:0] immediate,
  output [25:0] address
);


  assign address = instruction[25:0];
  assign funct = instruction[5:0];
  assign immediate = instruction[15:0];
  assign opcode = instruction[31:26];
  assign rd = instruction[15:11];
  assign rs = instruction[25:21];
  assign rt = instruction[20:16];
  assign shamt = instruction[10:6];
endmodule

// pc calc
module PC_Calc (
  input  [31:0] Last_PC,
  input  [31:0] extimm,
  input  [25:0] address,
  input  [31:0] Rrs,
  input  jump,
  input  branch,
  output [31:0] nextpc
);

  wire [31:0] adder_1_out, adder_2_out, shifter_1_out;

  // Probe on Last_PC
  Shifter #(.width(32)) shifter_1 (.in(extimm), .\dist (5'b00010), .out(shifter_1_out));
  Adder #(.width(32)) adder_1 (.a(32'h4), .b(Last_PC), .out(adder_1_out));  // open: cin, cout
  // Probe on adder_1_out
  Adder #(.width(32)) adder_2 (.a(adder_1_out), .b(shifter_1_out), .out(adder_2_out));  // open: cin, cout
  // Probe on adder_2_out
  // Probe on {adder_1_out[31:28], address, 2'b00}
  // Probe on nextpc
  Multiplexer #(.select(2), .width(32), .enable("false")) multiplexer_1 (
    .in0(adder_1_out), .in1(adder_2_out), .in2({adder_1_out[31:28], address, 2'b00}), .in3(Rrs),
    .out(nextpc), .sel({jump, branch}));
endmodule

// control
module Control (
  input  [5:0] opcode,
  input  [5:0] funct,
  input  [4:0] shamt,
  input  zero,
  output NoInst,
  output RegDst,
  output RegWr,
  output ExtOp,
  output MemWr,
  output Mem2Reg,
  output ALUsrc,
  output branch,
  output jump,
  output [5:0] ALUctr
);

  wire and_1_out, and_2_out, and_3_out, and_4_out, and_5_out, and_6_out, and_7_out, and_8_out, and_9_out,
       and_10_out, and_11_out, and_12_out, and_13_out, and_14_out, and_15_out, and_16_out, and_17_out,
       and_18_out, and_19_out, and_20_out, nor_1_out, not_1_out, not_2_out, not_3_out, not_4_out, not_5_out,
       not_6_out, not_7_out, not_8_out, not_9_out, not_10_out, not_11_out, not_12_out, not_13_out,
       not_14_out, or_1_out, or_2_out, or_3_out, undriven;

  nor nor_1 (nor_1_out, shamt[0], shamt[1], shamt[2], shamt[3], shamt[4]);
  not not_1 (not_1_out, zero);
  // Probe on funct
  // Probe on opcode
  not not_2 (not_2_out, funct[5]);
  not not_3 (not_3_out, funct[1]);
  not not_4 (not_4_out, funct[2]);
  not not_5 (not_5_out, funct[4]);
  not not_6 (not_6_out, funct[3]);
  not not_7 (not_7_out, opcode[5]);
  not not_8 (not_8_out, opcode[4]);
  not not_9 (not_9_out, opcode[3]);
  not not_10 (not_10_out, funct[0]);
  not not_11 (not_11_out, opcode[2]);
  not not_12 (not_12_out, opcode[0]);
  not not_13 (not_13_out, opcode[1]);
  and and_1 (and_1_out, not_12_out, not_12_out, not_13_out, not_11_out, not_9_out, not_8_out, not_7_out);
  and and_2 (and_2_out, and_1_out, not_3_out, not_4_out, not_6_out, not_5_out, funct[5]);
  and and_3 (and_3_out, and_1_out, not_10_out, funct[1], not_4_out, not_6_out, not_5_out, funct[5]);
  and and_4 (and_4_out, opcode[0], opcode[0], not_13_out, opcode[2], opcode[3], not_8_out, not_7_out);
  and and_5 (and_5_out, opcode[0], opcode[0], opcode[1], not_11_out, not_9_out, not_8_out, opcode[5]);
  and and_6 (and_6_out, opcode[0], opcode[0], opcode[1], not_11_out, opcode[3], not_8_out, opcode[5]);
  and and_7 (and_7_out, zero, not_12_out, not_13_out, opcode[2], not_9_out, not_8_out, not_7_out);
  and and_8 (and_8_out, not_12_out, not_12_out, opcode[1], not_11_out, not_9_out, not_8_out, not_7_out);
  and and_9 (and_9_out, and_1_out, not_10_out, not_3_out, not_4_out, funct[3], not_5_out, not_2_out);
  and and_10 (and_10_out, and_1_out, not_10_out, not_3_out, funct[2], not_6_out, not_5_out, funct[5]);
  and and_11 (and_11_out, and_1_out, funct[0], not_3_out, funct[2], not_6_out, not_5_out, funct[5]);
  and and_12 (and_12_out, not_12_out, not_12_out, not_13_out, opcode[2], opcode[3], not_8_out, not_7_out);
  and and_13 (and_13_out, not_13_out, not_11_out, opcode[3], not_8_out, not_7_out);
  and and_14 (and_14_out, and_1_out, not_10_out, not_3_out, not_4_out, not_6_out, not_5_out, not_2_out);
  not not_14 (not_14_out, nor_1_out);
  and and_15 (and_15_out, opcode[0], opcode[0], opcode[1], opcode[2], opcode[3], not_8_out, not_7_out);
  and and_16 (and_16_out, not_1_out, opcode[0], not_13_out, opcode[2], not_9_out, not_8_out, not_7_out);
  and and_17 (and_17_out, and_1_out, funct[0], not_3_out, funct[2], not_6_out, not_5_out, funct[5]);
  and and_18 (and_18_out, and_14_out, not_14_out);
  and and_19 (and_19_out, and_14_out, nor_1_out);
  buf or_1 (or_1_out, and_15_out);  // OR_Gate
  nor nor_2 (NoInst, or_2_out, or_3_out);
  or or_2 (or_2_out, undriven, and_16_out, and_15_out, and_18_out, and_13_out, and_12_out, and_11_out);
  or or_3 (or_3_out, and_10_out, and_9_out, and_8_out, and_7_out, and_6_out, and_5_out, and_4_out, and_3_out, and_2_out);
  or or_4 (RegDst, and_2_out, and_3_out, and_10_out, and_11_out, 1'b0);
  or or_5 (RegWr, and_2_out, and_3_out, and_4_out, and_5_out, and_10_out, and_11_out, and_12_out, and_13_out, or_1_out);
  or or_6 (ExtOp, and_5_out, and_6_out, and_7_out, and_13_out, and_16_out, 1'b0);
  or or_7 (MemWr, and_6_out, 1'b0);
  or or_8 (Mem2Reg, and_5_out, 1'b0);
  or or_9 (ALUsrc, and_4_out, and_5_out, and_6_out, and_12_out, and_13_out, 1'b0);
  buf and_20 (and_20_out, and_7_out);  // AND_Gate
  or or_10 (jump, and_8_out, and_9_out, 1'b0);
  or or_11 (ALUctr[0], and_2_out, and_4_out, and_5_out, and_6_out, and_11_out, and_13_out, 1'b0);
  or or_12 (ALUctr[1], and_2_out, and_5_out, and_6_out, and_13_out, 1'b0);
  or or_13 (ALUctr[2], and_3_out, 1'b0);
  buf or_14 (ALUctr[3], 1'b0);  // OR_Gate
  buf or_15 (ALUctr[4], 1'b0);  // OR_Gate
  buf or_16 (ALUctr[5], 1'b0);  // OR_Gate
  or or_17 (branch, and_20_out, and_16_out, and_9_out, 1'b0);
  DotMatrix #(.matrixcols(1), .matrixrows(6)) dotmatrix_1 (.col0(ALUctr));

  // Notes on the sheet:
  //   R format
  //   ADD
  //   ADD
  //   ADD
  //   ADD
  //   ADDU
  //   ADDU
  //   ADDU
  //   ADDU
  //   SUB
  //   ORI
  //   LW
  //   SW
  //   BEQ
  //   J
  //   JR
  //   AND
  //   OR
  //   ANDI
  //   ADDI
  //   ADDIU
  //   SLL
  //   LUI
  //   BNE
  //   MOVE
  //   NOOP
endmodule

module ALU (
  input  [31:0] BusA,
  input  [31:0] BusB,
  input  [5:0] ALUctr,
  output ALUeq,
  output [31:0] ALUout
);

  wire comparator_1_gt, comparator_1_lt, comparator_2_gt, comparator_2_lt, multiplexer_1_out;
  wire [31:0] adder_1_out, and_1_out, divider_1_out, divider_1_rem, multiplexer_2_out, multiplexer_3_out,
       multiplier_1_cout, multiplier_1_out, negator_1_out, or_1_out, shifter_1_out, shifter_2_out,
       shifter_3_out, subtractor_1_out, xor_1_out;

  // Probe on BusA
  // Probe on BusB
  Multiplier #(.width(32)) multiplier_1 (
    .a(BusA), .b(BusB), .out(multiplier_1_out), .cout(multiplier_1_cout));  // open: cin
  Divider #(.width(32)) divider_1 (.out(divider_1_out), .rem(divider_1_rem));  // open: a, b, upper
  Negator #(.width(32)) negator_1 (.in(BusA), .out(negator_1_out));
  Subtractor #(.width(32)) subtractor_1 (.a(BusA), .b(BusB), .out(subtractor_1_out), .bin(1'b0));  // open: bout
  Shifter #(.width(32)) shifter_1 (.in(BusA), .\dist (BusB[4:0]), .out(shifter_1_out));
  Shifter #(.width(32), .shift("lr")) shifter_2 (.in(BusA), .\dist (BusB[4:0]), .out(shifter_2_out));
  Shifter #(.width(32), .shift("ar")) shifter_3 (.in(BusA), .\dist (BusB[4:0]), .out(shifter_3_out));
  Comparator #(.width(32)) comparator_1 (.a(BusA), .b(BusB), .gt(comparator_1_gt), .eq(ALUeq), .lt(comparator_1_lt));
  Comparator #(.width(32), .mode("unsigned")) comparator_2 (
    .a(BusA), .b(BusB), .gt(comparator_2_gt), .eq(ALUeq), .lt(comparator_2_lt));
  assign and_1_out = BusA & BusB;  // AND_Gate and_1, 32 bits wide
  assign or_1_out = BusA | BusB;  // OR_Gate or_1, 32 bits wide
  assign xor_1_out = BusA ^ BusB;  // XOR_Gate xor_1, 32 bits wide
  Adder #(.width(32)) adder_1 (.a(BusA), .b(BusB), .out(adder_1_out), .cin(1'b0));  // open: cout
  Multiplexer #(.select(4), .enable("false")) multiplexer_1 (
    .in11(ALUeq), .in12(comparator_1_gt), .in13(comparator_1_lt), .in14(comparator_2_gt),
    .in15(comparator_2_lt), .out(multiplexer_1_out), .sel(ALUctr[3:0]));  // open: in0, in1, in2, in3, in4, in5, in6, in7, in8, in9, in10
  Multiplexer #(.select(4), .width(32), .enable("false")) multiplexer_2 (
    .in8(multiplier_1_cout), .in9(divider_1_rem), .out(multiplexer_2_out), .sel(ALUctr[3:0]));  // open: in0, in1, in2, in3, in4, in5, in6, in7, in10, in11, in12, in13, in14, in15
  Multiplexer #(.select(4), .width(32), .enable("false")) multiplexer_3 (
    .in0(and_1_out), .in1(or_1_out), .in2(xor_1_out), .in3(adder_1_out), .in4(subtractor_1_out),
    .in5(shifter_1_out), .in6(shifter_2_out), .in7(shifter_3_out), .in8(multiplier_1_out),
    .in9(divider_1_out), .in10(negator_1_out), .out(multiplexer_3_out), .sel(ALUctr[3:0]));  // open: in11, in12, in13, in14, in15
  Multiplexer #(.select(2), .width(32), .enable("false")) multiplexer_4 (
    .in0(multiplexer_3_out), .out(ALUout), .sel(ALUctr[5:4]));  // open: in1, in2, in3
  // Probe on ALUout

  // Notes on the sheet:
  //   1000 MULT
  //   1001 DIV
  //   100 SUB
  //   101 SLL
  //   110 SRL
  //   111 SRA
  //   0 AND
  //   1 OR
  //   10 XOR
  //   11 ADD
endmodule

// BSel
module Bank_Select (
  input  [5:0] Bank,
  input  [31:0] addr,
  output [31:0] addr_2,
  output [23:0] waddr,
  output select,
  output SIGBUS
);

  Comparator #(.width(6), .mode("unsigned")) comparator_1 (.a(Bank), .b(addr[31:26]), .eq(select));  // open: gt, lt
  or or_1 (SIGBUS, addr[1], addr[0]);
  assign addr_2 = select ? addr : 32'bz;  // Controlled_Buffer controlled_buffer_1
  assign waddr = select ? addr[25:2] : 24'bz;  // Controlled_Buffer controlled_buffer_2
endmodule

// RegFile
module Register_File (
  input  [4:0] Ra,
  input  [4:0] Rb,
  input  RegWr,
  input  [4:0] Rw,
  input  [31:0] busW,
  input  clk,
  input  clr,
  output [31:0] t1,
  output [31:0] t2,
  output [31:0] t3,
  output [31:0] BusA,
  output [31:0] BusB
);

  wire demultiplexer_1_out0, demultiplexer_1_out1, demultiplexer_2_out0, demultiplexer_2_out1,
       demultiplexer_2_out2, demultiplexer_2_out3, demultiplexer_2_out4, demultiplexer_2_out5,
       demultiplexer_2_out6, demultiplexer_2_out7, demultiplexer_2_out8, demultiplexer_2_out9,
       demultiplexer_2_out10, demultiplexer_2_out11, demultiplexer_2_out12, demultiplexer_2_out13,
       demultiplexer_2_out14, demultiplexer_2_out15, demultiplexer_3_out0, demultiplexer_3_out1,
       demultiplexer_3_out2, demultiplexer_3_out3, demultiplexer_3_out4, demultiplexer_3_out5,
       demultiplexer_3_out6, demultiplexer_3_out7, demultiplexer_3_out8, demultiplexer_3_out9,
       demultiplexer_3_out10, demultiplexer_3_out11, demultiplexer_3_out12, demultiplexer_3_out13,
       demultiplexer_3_out14, demultiplexer_3_out15;
  wire [31:0] _0_q, _1_q, _2_q, _3_q, _4_q, _5_q, _6_q, _7_q, _11_q, _12_q, _13_q, _14_q, _15_q, _16_q,
       _17_q, _18_q, _19_q, _20_q, _21_q, _22_q, _23_q, _24_q, _25_q, _26_q, _27_q, _28_q, _29_q, _30_q,
       _31_q, multiplexer_1_out, multiplexer_2_out, multiplexer_3_out, multiplexer_4_out;

  Demultiplexer #(.enable("false")) demultiplexer_1 (
    .out0(demultiplexer_1_out0), .out1(demultiplexer_1_out1), .in(RegWr), .sel(Rw[4]));
  Demultiplexer #(.select(4), .enable("false")) demultiplexer_2 (
    .out0(demultiplexer_2_out0), .out1(demultiplexer_2_out1), .out2(demultiplexer_2_out2),
    .out3(demultiplexer_2_out3), .out4(demultiplexer_2_out4), .out5(demultiplexer_2_out5),
    .out6(demultiplexer_2_out6), .out7(demultiplexer_2_out7), .out8(demultiplexer_2_out8),
    .out9(demultiplexer_2_out9), .out10(demultiplexer_2_out10), .out11(demultiplexer_2_out11),
    .out12(demultiplexer_2_out12), .out13(demultiplexer_2_out13), .out14(demultiplexer_2_out14),
    .out15(demultiplexer_2_out15), .in(demultiplexer_1_out0), .sel(Rw[3:0]));
  Demultiplexer #(.select(4), .enable("false")) demultiplexer_3 (
    .out0(demultiplexer_3_out0), .out1(demultiplexer_3_out1), .out2(demultiplexer_3_out2),
    .out3(demultiplexer_3_out3), .out4(demultiplexer_3_out4), .out5(demultiplexer_3_out5),
    .out6(demultiplexer_3_out6), .out7(demultiplexer_3_out7), .out8(demultiplexer_3_out8),
    .out9(demultiplexer_3_out9), .out10(demultiplexer_3_out10), .out11(demultiplexer_3_out11),
    .out12(demultiplexer_3_out12), .out13(demultiplexer_3_out13), .out14(demultiplexer_3_out14),
    .out15(demultiplexer_3_out15), .in(demultiplexer_1_out1), .sel(Rw[3:0]));
  Register #(.width(32)) _0 (.D(busW), .en(demultiplexer_2_out0), .Q(_0_q), .clk(clk), .clr(clr));
  Register #(.width(32)) _4 (.D(busW), .en(demultiplexer_2_out4), .Q(_4_q), .clk(clk), .clr(clr));
  Register #(.width(32)) _8 (.D(busW), .en(demultiplexer_2_out8), .Q(t1), .clk(clk), .clr(clr));
  Register #(.width(32)) _12 (.D(busW), .en(demultiplexer_2_out12), .Q(_12_q), .clk(clk), .clr(clr));
  Register #(.width(32)) _16 (.D(busW), .en(demultiplexer_3_out0), .Q(_16_q), .clk(clk), .clr(clr));
  Register #(.width(32)) _20 (.D(busW), .en(demultiplexer_3_out4), .Q(_20_q), .clk(clk), .clr(clr));
  Register #(.width(32)) _24 (.D(busW), .en(demultiplexer_3_out8), .Q(_24_q), .clk(clk), .clr(clr));
  Register #(.width(32)) _28 (.D(busW), .en(demultiplexer_3_out12), .Q(_28_q), .clk(clk), .clr(clr));
  Register #(.width(32)) _1 (.D(busW), .en(demultiplexer_2_out1), .Q(_1_q), .clk(clk), .clr(clr));
  Register #(.width(32)) _5 (.D(busW), .en(demultiplexer_2_out5), .Q(_5_q), .clk(clk), .clr(clr));
  Register #(.width(32)) _9 (.D(busW), .en(demultiplexer_2_out9), .Q(t2), .clk(clk), .clr(clr));
  Register #(.width(32)) _13 (.D(busW), .en(demultiplexer_2_out13), .Q(_13_q), .clk(clk), .clr(clr));
  Register #(.width(32)) _17 (.D(busW), .en(demultiplexer_3_out1), .Q(_17_q), .clk(clk), .clr(clr));
  Register #(.width(32)) _21 (.D(busW), .en(demultiplexer_3_out5), .Q(_21_q), .clk(clk), .clr(clr));
  Register #(.width(32)) _25 (.D(busW), .en(demultiplexer_3_out9), .Q(_25_q), .clk(clk), .clr(clr));
  Register #(.width(32)) _29 (.D(busW), .en(demultiplexer_3_out13), .Q(_29_q), .clk(clk), .clr(clr));
  Register #(.width(32)) _2 (.D(busW), .en(demultiplexer_2_out2), .Q(_2_q), .clk(clk), .clr(clr));
  Register #(.width(32)) _6 (.D(busW), .en(demultiplexer_2_out6), .Q(_6_q), .clk(clk), .clr(clr));
  Register #(.width(32)) _10 (.D(busW), .en(demultiplexer_2_out10), .Q(t3), .clk(clk), .clr(clr));
  Register #(.width(32)) _14 (.D(busW), .en(demultiplexer_2_out14), .Q(_14_q), .clk(clk), .clr(clr));
  Register #(.width(32)) _18 (.D(busW), .en(demultiplexer_3_out2), .Q(_18_q), .clk(clk), .clr(clr));
  Register #(.width(32)) _22 (.D(busW), .en(demultiplexer_3_out6), .Q(_22_q), .clk(clk), .clr(clr));
  Register #(.width(32)) _26 (.D(busW), .en(demultiplexer_3_out10), .Q(_26_q), .clk(clk), .clr(clr));
  Register #(.width(32)) _30 (.D(busW), .en(demultiplexer_3_out14), .Q(_30_q), .clk(clk), .clr(clr));
  Register #(.width(32)) _3 (.D(busW), .en(demultiplexer_2_out3), .Q(_3_q), .clk(clk), .clr(clr));
  Register #(.width(32)) _7 (.D(busW), .en(demultiplexer_2_out7), .Q(_7_q), .clk(clk), .clr(clr));
  Register #(.width(32)) _11 (.D(busW), .en(demultiplexer_2_out11), .Q(_11_q), .clk(clk), .clr(clr));
  Register #(.width(32)) _15 (.D(busW), .en(demultiplexer_2_out15), .Q(_15_q), .clk(clk), .clr(clr));
  Register #(.width(32)) _19 (.D(busW), .en(demultiplexer_3_out3), .Q(_19_q), .clk(clk), .clr(clr));
  Register #(.width(32)) _23 (.D(busW), .en(demultiplexer_3_out7), .Q(_23_q), .clk(clk), .clr(clr));
  Register #(.width(32)) _27 (.D(busW), .en(demultiplexer_3_out11), .Q(_27_q), .clk(clk), .clr(clr));
  Register #(.width(32)) _31 (.D(busW), .en(demultiplexer_3_out15), .Q(_31_q), .clk(clk), .clr(clr));
  DotMatrix #(.matrixcols(32), .matrixrows(32)) dotmatrix_1 (
    .col0(_31_q), .col1(_30_q), .col2(_29_q), .col3(_28_q), .col4(_27_q), .col5(_26_q), .col6(_25_q),
    .col7(_24_q), .col8(_23_q), .col9(_22_q), .col10(_21_q), .col11(_20_q), .col12(_19_q), .col13(_18_q),
    .col14(_17_q), .col15(_16_q), .col16(_15_q), .col17(_14_q), .col18(_13_q), .col19(_12_q), .col20(_11_q),
    .col21(t3), .col22(t2), .col23(t1), .col24(_7_q), .col25(_6_q), .col26(_5_q), .col27(_4_q), .col28(_3_q),
    .col29(_2_q), .col30(_1_q), .col31({32{1'b0}}));
  Multiplexer #(.select(4), .width(32), .enable("false")) multiplexer_1 (
    .in0({32{1'b0}}), .in1(_1_q), .in2(_2_q), .in3(_3_q), .in4(_4_q), .in5(_5_q), .in6(_6_q), .in7(_7_q),
    .in8(t1), .in9(t2), .in10(t3), .in11(_11_q), .in12(_12_q), .in13(_13_q), .in14(_14_q), .in15(_15_q),
    .out(multiplexer_1_out), .sel(Ra[3:0]));
  Multiplexer #(.select(4), .width(32), .enable("false")) multiplexer_2 (
    .in0(_16_q), .in1(_17_q), .in2(_18_q), .in3(_19_q), .in4(_20_q), .in5(_21_q), .in6(_22_q), .in7(_23_q),
    .in8(_24_q), .in9(_25_q), .in10(_26_q), .in11(_27_q), .in12(_28_q), .in13(_29_q), .in14(_30_q),
    .in15(_31_q), .out(multiplexer_2_out), .sel(Ra[3:0]));
  Multiplexer #(.select(4), .width(32), .enable("false")) multiplexer_3 (
    .in0({32{1'b0}}), .in1(_1_q), .in2(_2_q), .in3(_3_q), .in4(_4_q), .in5(_5_q), .in6(_6_q), .in7(_7_q),
    .in8(t1), .in9(t2), .in10(t3), .in11(_11_q), .in12(_12_q), .in13(_13_q), .in14(_14_q), .in15(_15_q),
    .out(multiplexer_3_out), .sel(Rb[3:0]));
  Multiplexer #(.select(4), .width(32), .enable("false")) multiplexer_4 (
    .in0(_16_q), .in1(_17_q), .in2(_18_q), .in3(_19_q), .in4(_20_q), .in5(_21_q), .in6(_22_q), .in7(_23_q),
    .in8(_24_q), .in9(_25_q), .in10(_26_q), .in11(_27_q), .in12(_28_q), .in13(_29_q), .in14(_30_q),
    .in15(_31_q), .out(multiplexer_4_out), .sel(Rb[3:0]));
  Multiplexer #(.width(32), .enable("false")) multiplexer_5 (
    .in0(multiplexer_1_out), .in1(multiplexer_2_out), .out(BusA), .sel(Ra[4]));
  Multiplexer #(.width(32), .enable("false")) multiplexer_6 (
    .in0(multiplexer_3_out), .in1(multiplexer_4_out), .out(BusB), .sel(Rb[4]));

  // Notes on the sheet:
  //   $0 is ALWAYS ZERO
endmodule

// Ext
module Extender (
  input  [15:0] Input,
  input  Sign,
  output [31:0] Output
);

  and and_1 (Output[31], Input[15], Sign);

  assign Output[30:0] = {{15{Output[31]}}, Input};
endmodule

// PC Calc
module PC_Calc_w__Delay (
  input  [31:0] Last_PC,
  input  [31:0] extimm,
  input  [25:0] address,
  input  Clr,
  input  [31:0] Rrs,
  input  Clk,
  input  jump,
  input  branch,
  output [31:0] nextpc
);

  wire d_ff_1_q, or_1_out;
  wire [31:0] adder_1_out, adder_2_out, multiplexer_1_out, register_1_q, shifter_1_out;

  // Probe on Last_PC
  Shifter #(.width(32)) shifter_1 (.in(extimm), .\dist (5'b00010), .out(shifter_1_out));
  Adder #(.width(32)) adder_1 (.a(32'h4), .b(Last_PC), .out(adder_1_out));  // open: cin, cout
  // Probe on adder_1_out
  Adder #(.width(32)) adder_2 (.a(adder_1_out), .b(shifter_1_out), .out(adder_2_out));  // open: cin, cout
  // Probe on adder_2_out
  // Probe on {adder_1_out[31:28], address, 2'b00}
  // Probe on multiplexer_1_out
  Multiplexer #(.select(2), .width(32), .enable("false")) multiplexer_1 (
    .in0(adder_1_out), .in1(adder_2_out), .in2({adder_1_out[31:28], address, 2'b00}), .in3(Rrs),
    .out(multiplexer_1_out), .sel({jump, branch}));
  or or_1 (or_1_out, jump, branch);
  D_Flip_Flop d_ff_1 (.clk(Clk), .D(or_1_out), .Q(d_ff_1_q), .en(1'b1), .reset(Clr));  // open: Qn, preset
  Register #(.width(32)) register_1 (.D(multiplexer_1_out), .en(or_1_out), .Q(register_1_q), .clk(Clk));  // open: clr
  Multiplexer #(.width(32), .enable("false")) multiplexer_2 (
    .in0(adder_1_out), .in1(register_1_q), .out(nextpc), .sel(d_ff_1_q));
  // Probe on nextpc
endmodule

module Joystick (
);

  wire [3:0] joystick_1_x, joystick_1_y;
  wire [14:0] decoder_1_out15, demultiplexer_1_out1, demultiplexer_1_out2, demultiplexer_1_out3,
       demultiplexer_1_out4, demultiplexer_1_out5, demultiplexer_1_out6, demultiplexer_1_out7,
       demultiplexer_1_out8, demultiplexer_1_out9, demultiplexer_1_out10, demultiplexer_1_out11,
       demultiplexer_1_out12, demultiplexer_1_out13, demultiplexer_1_out14, demultiplexer_1_out15;

  // Probe on joystick_1_x
  Joystick_part joystick_1 (.x(joystick_1_x), .y(joystick_1_y));
  Decoder #(.select(4), .enable("false")) decoder_1 (
    .out1(decoder_1_out15[14]), .out2(decoder_1_out15[13]), .out3(decoder_1_out15[12]),
    .out4(decoder_1_out15[11]), .out5(decoder_1_out15[10]), .out6(decoder_1_out15[9]),
    .out7(decoder_1_out15[8]), .out8(decoder_1_out15[7]), .out9(decoder_1_out15[6]),
    .out10(decoder_1_out15[5]), .out11(decoder_1_out15[4]), .out12(decoder_1_out15[3]),
    .out13(decoder_1_out15[2]), .out14(decoder_1_out15[1]), .out15(decoder_1_out15[0]), .sel(joystick_1_y));  // open: out0
  // Probe on joystick_1_y
  DotMatrix #(.matrixcols(15), .matrixrows(15)) dotmatrix_1 (
    .col0(demultiplexer_1_out1), .col1(demultiplexer_1_out2), .col2(demultiplexer_1_out3),
    .col3(demultiplexer_1_out4), .col4(demultiplexer_1_out5), .col5(demultiplexer_1_out6),
    .col6(demultiplexer_1_out7), .col7(demultiplexer_1_out8), .col8(demultiplexer_1_out9),
    .col9(demultiplexer_1_out10), .col10(demultiplexer_1_out11), .col11(demultiplexer_1_out12),
    .col12(demultiplexer_1_out13), .col13(demultiplexer_1_out14), .col14(demultiplexer_1_out15));
  Demultiplexer #(.select(4), .width(15), .enable("false")) demultiplexer_1 (
    .out1(demultiplexer_1_out1), .out2(demultiplexer_1_out2), .out3(demultiplexer_1_out3),
    .out4(demultiplexer_1_out4), .out5(demultiplexer_1_out5), .out6(demultiplexer_1_out6),
    .out7(demultiplexer_1_out7), .out8(demultiplexer_1_out8), .out9(demultiplexer_1_out9),
    .out10(demultiplexer_1_out10), .out11(demultiplexer_1_out11), .out12(demultiplexer_1_out12),
    .out13(demultiplexer_1_out13), .out14(demultiplexer_1_out14), .out15(demultiplexer_1_out15),
    .in(decoder_1_out15), .sel(joystick_1_x));  // open: out0
endmodule

module D_flip_flop (
  input  D,
  input  Clk,
  output Q,
  output nQ
);

  wire nand_1_out, nand_2_out, nand_3_out, nand_4_out;

  nand nand_1 (nand_1_out, nand_4_out, nand_2_out);
  nand nand_2 (nand_2_out, nand_1_out, Clk);
  nand nand_3 (nand_3_out, nand_2_out, Clk, nand_4_out);
  nand nand_4 (nand_4_out, nand_3_out, D);
  nand nand_5 (Q, nand_2_out, nQ);
  nand nand_6 (nQ, Q, nand_3_out);
endmodule

module Control2 (
  input  [5:0] opcode,
  input  [5:0] funct,
  output Branch,
  output Jump,
  output RegDst,
  output RegWr,
  output ExtOp,
  output MemWr,
  output Mem2Reg,
  output ALUsrc
);

  wire decoder_1_out0, decoder_1_out1, decoder_1_out2, decoder_1_out3, decoder_1_out4, decoder_1_out5,
       decoder_1_out6, decoder_1_out7, demultiplexer_1_out0, demultiplexer_1_out1, demultiplexer_1_out2,
       demultiplexer_1_out3, demultiplexer_1_out4, demultiplexer_1_out5, demultiplexer_1_out6,
       demultiplexer_1_out7, demultiplexer_2_out0, demultiplexer_2_out2, demultiplexer_2_out3,
       demultiplexer_2_out4, demultiplexer_2_out5, demultiplexer_3_out0, demultiplexer_3_out1,
       demultiplexer_3_out4, demultiplexer_3_out5, demultiplexer_3_out6, demultiplexer_3_out7,
       demultiplexer_6_out0, demultiplexer_6_out1, demultiplexer_6_out3, demultiplexer_6_out4,
       demultiplexer_6_out5, demultiplexer_7_out0, demultiplexer_7_out1, demultiplexer_7_out3,
       demultiplexer_10_out0, demultiplexer_10_out2, demultiplexer_10_out3, demultiplexer_11_out0,
       demultiplexer_11_out1, demultiplexer_12_out0, demultiplexer_12_out1, demultiplexer_12_out2,
       demultiplexer_12_out3, demultiplexer_13_out0, demultiplexer_13_out1, demultiplexer_13_out2,
       demultiplexer_13_out3, demultiplexer_14_out0, demultiplexer_14_out1, demultiplexer_14_out2,
       demultiplexer_14_out3, demultiplexer_14_out4, demultiplexer_14_out5, demultiplexer_14_out6,
       demultiplexer_14_out7, or_1_out, or_2_out, or_4_out, or_5_out, or_7_out, or_8_out, or_10_out,
       or_11_out, or_13_out, or_14_out, or_16_out, or_17_out, or_21_out, or_22_out, or_23_out, or_24_out;
  wire [5:0] alu_encoder_1_aluctr;
  wire [15:0] undriven;

  Decoder #(.select(3), .enable("false")) decoder_1 (
    .out0(decoder_1_out0), .out1(decoder_1_out1), .out2(decoder_1_out2), .out3(decoder_1_out3),
    .out4(decoder_1_out4), .out5(decoder_1_out5), .out6(decoder_1_out6), .out7(decoder_1_out7),
    .sel(opcode[5:3]));
  Demultiplexer #(.select(3), .enable("false")) demultiplexer_1 (
    .out0(demultiplexer_1_out0), .out1(demultiplexer_1_out1), .out2(demultiplexer_1_out2),
    .out3(demultiplexer_1_out3), .out4(demultiplexer_1_out4), .out5(demultiplexer_1_out5),
    .out6(demultiplexer_1_out6), .out7(demultiplexer_1_out7), .in(demultiplexer_2_out0), .sel(funct[5:3]));
  Demultiplexer #(.select(3), .enable("false")) demultiplexer_2 (
    .out0(demultiplexer_2_out0), .out2(demultiplexer_2_out2), .out3(demultiplexer_2_out3),
    .out4(demultiplexer_2_out4), .out5(demultiplexer_2_out5), .in(decoder_1_out0), .sel(opcode[2:0]));  // open: out1, out6, out7
  Demultiplexer #(.select(3), .enable("false")) demultiplexer_3 (
    .out0(demultiplexer_3_out0), .out1(demultiplexer_3_out1), .out4(demultiplexer_3_out4),
    .out5(demultiplexer_3_out5), .out6(demultiplexer_3_out6), .out7(demultiplexer_3_out7),
    .in(decoder_1_out1), .sel(opcode[2:0]));  // open: out2, out3
  Demultiplexer #(.select(3), .enable("false")) demultiplexer_4 (
    .in(decoder_1_out2), .sel(opcode[2:0]));  // open: out0, out1, out2, out3, out4, out5, out6, out7
  Demultiplexer #(.select(3), .enable("false")) demultiplexer_5 (
    .in(decoder_1_out3), .sel(opcode[2:0]));  // open: out0, out1, out2, out3, out4, out5, out6, out7
  Demultiplexer #(.select(3), .enable("false")) demultiplexer_6 (
    .out0(demultiplexer_6_out0), .out1(demultiplexer_6_out1), .out3(demultiplexer_6_out3),
    .out4(demultiplexer_6_out4), .out5(demultiplexer_6_out5), .in(decoder_1_out4), .sel(opcode[2:0]));  // open: out2, out6, out7
  Demultiplexer #(.select(3), .enable("false")) demultiplexer_7 (
    .out0(demultiplexer_7_out0), .out1(demultiplexer_7_out1), .out3(demultiplexer_7_out3),
    .in(decoder_1_out5), .sel(opcode[2:0]));  // open: out2, out4, out5, out6, out7
  Demultiplexer #(.select(3), .enable("false")) demultiplexer_8 (
    .in(decoder_1_out6), .sel(opcode[2:0]));  // open: out0, out1, out2, out3, out4, out5, out6, out7
  Demultiplexer #(.select(3), .enable("false")) demultiplexer_9 (
    .in(decoder_1_out7), .sel(opcode[2:0]));  // open: out0, out1, out2, out3, out4, out5, out6, out7
  Demultiplexer #(.select(3), .enable("false")) demultiplexer_10 (
    .out0(demultiplexer_10_out0), .out2(demultiplexer_10_out2), .out3(demultiplexer_10_out3),
    .in(demultiplexer_1_out0), .sel(funct[2:0]));  // open: out1, out4, out5, out6, out7
  Demultiplexer #(.select(3), .enable("false")) demultiplexer_11 (
    .out0(demultiplexer_11_out0), .out1(demultiplexer_11_out1), .in(demultiplexer_1_out1), .sel(funct[2:0]));  // open: out2, out3, out4, out5, out6, out7
  Demultiplexer #(.select(3), .enable("false")) demultiplexer_12 (
    .out0(demultiplexer_12_out0), .out1(demultiplexer_12_out1), .out2(demultiplexer_12_out2),
    .out3(demultiplexer_12_out3), .in(demultiplexer_1_out2), .sel(funct[2:0]));  // open: out4, out5, out6, out7
  Demultiplexer #(.select(3), .enable("false")) demultiplexer_13 (
    .out0(demultiplexer_13_out0), .out1(demultiplexer_13_out1), .out2(demultiplexer_13_out2),
    .out3(demultiplexer_13_out3), .in(demultiplexer_1_out3), .sel(funct[2:0]));  // open: out4, out5, out6, out7
  Demultiplexer #(.select(3), .enable("false")) demultiplexer_14 (
    .out0(demultiplexer_14_out0), .out1(demultiplexer_14_out1), .out2(demultiplexer_14_out2),
    .out3(demultiplexer_14_out3), .out4(demultiplexer_14_out4), .out5(demultiplexer_14_out5),
    .out6(demultiplexer_14_out6), .out7(demultiplexer_14_out7), .in(demultiplexer_1_out4), .sel(funct[2:0]));
  Demultiplexer #(.select(3), .enable("false")) demultiplexer_15 (
    .in(demultiplexer_1_out5), .sel(funct[2:0]));  // open: out0, out1, out2, out3, out4, out5, out6, out7
  Demultiplexer #(.select(3), .enable("false")) demultiplexer_16 (
    .in(demultiplexer_1_out6), .sel(funct[2:0]));  // open: out0, out1, out2, out3, out4, out5, out6, out7
  Demultiplexer #(.select(3), .enable("false")) demultiplexer_17 (
    .in(demultiplexer_1_out7), .sel(funct[2:0]));  // open: out0, out1, out2, out3, out4, out5, out6, out7
  buf or_1 (or_1_out, 1'b0);  // OR_Gate
  buf or_2 (or_2_out, or_24_out);  // OR_Gate
  or or_3 (RegDst, or_1_out, or_2_out);
  or or_4 (or_4_out, demultiplexer_11_out1, demultiplexer_2_out3);
  or or_5 (or_5_out, or_22_out, or_24_out, or_21_out);
  or or_6 (RegWr, or_4_out, or_5_out);
  buf or_7 (or_7_out, 1'b0);  // OR_Gate
  or or_8 (or_8_out, or_21_out, or_22_out, or_23_out);
  or or_9 (ExtOp, or_7_out, or_8_out);
  buf or_10 (or_10_out, 1'b0);  // OR_Gate
  buf or_11 (or_11_out, or_23_out);  // OR_Gate
  or or_12 (MemWr, or_10_out, or_11_out);
  buf or_13 (or_13_out, 1'b0);  // OR_Gate
  buf or_14 (or_14_out, or_22_out);  // OR_Gate
  or or_15 (Mem2Reg, or_13_out, or_14_out);
  buf or_16 (or_16_out, 1'b0);  // OR_Gate
  or or_17 (or_17_out, or_23_out, or_22_out, or_21_out);
  or or_18 (ALUsrc, or_16_out, or_17_out);
  ALU_Encoder alu_encoder_1 (.F0(undriven), .ALUctr(alu_encoder_1_aluctr));  // open: F1, F2, F3
  or or_19 (Branch, demultiplexer_2_out4, demultiplexer_2_out5, demultiplexer_11_out0, demultiplexer_11_out1);
  or or_20 (Jump, demultiplexer_2_out2, demultiplexer_2_out3, demultiplexer_11_out0, demultiplexer_11_out1);
  or or_21 (or_21_out, demultiplexer_3_out7, demultiplexer_3_out6, demultiplexer_3_out5, demultiplexer_3_out4, demultiplexer_3_out1, demultiplexer_3_out0);
  or or_22 (or_22_out, demultiplexer_6_out5, demultiplexer_6_out4, demultiplexer_6_out3, demultiplexer_6_out1, demultiplexer_6_out0);
  or or_23 (or_23_out, demultiplexer_7_out3, demultiplexer_7_out1, demultiplexer_7_out0);
  or or_24 (or_24_out, demultiplexer_14_out7, demultiplexer_14_out6, demultiplexer_14_out5, demultiplexer_14_out4, demultiplexer_14_out3, demultiplexer_14_out2, demultiplexer_14_out1, demultiplexer_14_out0);

  // Notes on the sheet:
  //   RegDst
  //   RegWr
  //   ExtOp
  //   MemWr
  //   Mem2Reg
  //   Immed
  //   ALUsrc
  //   3Reg
  //   Loads
  //   Stores
  //   LB
  //   LH
  //   LW
  //   LBU
  //   LHU
  //   SB
  //   SH
  //   SW
  //   SLL
  //   SRL
  //   SRA
  //   JR
  //   JALR
  //   MFHI
  //   MTHI
  //   MFLO
  //   MTLO
  //   MULT
  //   MULTU
  //   DIV
  //   DIVU
  //   ADD
  //   ADDU
  //   SUB
  //   SUBU
  //   AND
  //   OR
  //   XOR
  //   NOR
  //   J
  //   JAL
  //   BEQ
  //   BNE
  //   ADDI
  //   ADDIU
  //   ANDI
  //   ORI
  //   XORI
  //   LUI
endmodule

module KB_Controller (
  input  Clk,
  input  Clr,
  input  Sel,
  input  Wr,
  input  Addr,
  output [10:0] out_6,
  output [7:0] Data
);

  wire [0:0] undriven;
  wire [6:0] multiplexer_1_out;
  wire [6:1] undriven_2;

  assign Data[6:0] = out_6[9] ? multiplexer_1_out : 7'bz;  // Controlled_Buffer controlled_buffer_1
  Multiplexer #(.width(7), .enable("false")) multiplexer_1 (
    .in0({undriven_2, out_6[7]}), .in1(out_6[6:0]), .out(multiplexer_1_out), .sel(undriven[0]));
  and and_1 (out_6[10], Clk, out_6[9], undriven[0]);
  // Pins of 7 and 8 bits meet at Data

  assign out_6[8] = Clr;
endmodule

// ALUenc
module ALU_Encoder (
  input  [15:0] F0,
  input  [15:0] F1,
  input  [15:0] F2,
  input  [15:0] F3,
  output [5:0] ALUctr
);

  wire priority_encoder_1_gs, priority_encoder_2_en_out, priority_encoder_2_gs, priority_encoder_3_en_out,
       priority_encoder_3_gs, priority_encoder_4_en_out, priority_encoder_4_gs;

  Priority_Encoder #(.select(4)) priority_encoder_1 (
    .in0(F0[0]), .in1(F0[1]), .in2(F0[2]), .in3(F0[3]), .in4(F0[4]), .in5(F0[5]), .in6(F0[6]), .in7(F0[7]),
    .in8(F0[8]), .in9(F0[9]), .in10(F0[10]), .in11(F0[11]), .in12(F0[12]), .in13(F0[13]), .in14(F0[14]),
    .in15(F0[15]), .out(ALUctr[3:0]), .gs(priority_encoder_1_gs), .en_in(priority_encoder_2_en_out));  // open: en_out
  Priority_Encoder #(.select(4)) priority_encoder_2 (
    .in0(F1[0]), .in1(F1[1]), .in2(F1[2]), .in3(F1[3]), .in4(F1[4]), .in5(F1[5]), .in6(F1[6]), .in7(F1[7]),
    .in8(F1[8]), .in9(F1[9]), .in10(F1[10]), .in11(F1[11]), .in12(F1[12]), .in13(F1[13]), .in14(F1[14]),
    .in15(F1[15]), .out(ALUctr[3:0]), .gs(priority_encoder_2_gs), .en_out(priority_encoder_2_en_out),
    .en_in(priority_encoder_3_en_out));
  Priority_Encoder #(.select(4)) priority_encoder_3 (
    .in0(F2[0]), .in1(F2[1]), .in2(F2[2]), .in3(F2[3]), .in4(F2[4]), .in5(F2[5]), .in6(F2[6]), .in7(F2[7]),
    .in8(F2[8]), .in9(F2[9]), .in10(F2[10]), .in11(F2[11]), .in12(F2[12]), .in13(F2[13]), .in14(F2[14]),
    .in15(F2[15]), .out(ALUctr[3:0]), .gs(priority_encoder_3_gs), .en_out(priority_encoder_3_en_out),
    .en_in(priority_encoder_4_en_out));
  Priority_Encoder #(.select(4)) priority_encoder_4 (
    .in0(F3[0]), .in1(F3[1]), .in2(F3[2]), .in3(F3[3]), .in4(F3[4]), .in5(F3[5]), .in6(F3[6]), .in7(F3[7]),
    .in8(F3[8]), .in9(F3[9]), .in10(F3[10]), .in11(F3[11]), .in12(F3[12]), .in13(F3[13]), .in14(F3[14]),
    .in15(F3[15]), .out(ALUctr[3:0]), .gs(priority_encoder_4_gs), .en_out(priority_encoder_4_en_out));  // open: en_in
  Priority_Encoder #(.select(2)) priority_encoder_5 (
    .in0(priority_encoder_1_gs), .in1(priority_encoder_2_gs), .in2(priority_encoder_3_gs),
    .in3(priority_encoder_4_gs), .out(ALUctr[5:4]));  // open: gs, en_out, en_in
endmodule

module ControlX (
  input  [5:0] opcode,
  input  [5:0] funct,
  output RegDst,
  output RegWr,
  output ExtOp,
  output MemWr,
  output Mem2Reg,
  output ALUsrc,
  output branch,
  output jump,
  output [5:0] ALUctr
);

  wire and_1_out, nor_1_out, nor_2_out, not_1_out, not_2_out, not_3_out, not_4_out;
  wire [15:14] rom_1_data;

  not not_1 (not_1_out, opcode[1]);
  not not_2 (not_2_out, opcode[2]);
  not not_3 (not_3_out, opcode[3]);
  not not_4 (not_4_out, opcode[5]);
  nor nor_1 (nor_1_out, opcode[0], opcode[1], opcode[2], opcode[3], opcode[4], opcode[5]);
  and and_1 (and_1_out, opcode[0], not_1_out, not_2_out, not_3_out, opcode[4], not_4_out);
  ROM #(.addrWidth(6), .dataWidth(16)) rom_1 (
    .addr(opcode), .data({rom_1_data, ALUctr, jump, branch, ALUsrc, Mem2Reg, MemWr, ExtOp, RegWr, RegDst}),
    .sel(nor_2_out));
  ROM #(.addrWidth(6), .dataWidth(16)) rom_2 (
    .addr(funct), .data({rom_1_data, ALUctr, jump, branch, ALUsrc, Mem2Reg, MemWr, ExtOp, RegWr, RegDst}),
    .sel(nor_1_out));
  ROM #(.addrWidth(6), .dataWidth(16)) rom_3 (
    .addr(funct), .data({rom_1_data, ALUctr, jump, branch, ALUsrc, Mem2Reg, MemWr, ExtOp, RegWr, RegDst}),
    .sel(and_1_out));
  nor nor_2 (nor_2_out, nor_1_out, and_1_out);
  // Probe on {rom_1_data, ALUctr, jump, branch, ALUsrc, Mem2Reg, MemWr, ExtOp, RegWr, RegDst}
  // Probe on {rom_1_data, ALUctr, jump, branch, ALUsrc, Mem2Reg, MemWr, ExtOp, RegWr, RegDst}

  // Notes on the sheet:
  //   opcode
  //   func
  //   float
  //   contents of rom_1 (hex, n*v repeats v):
  //   ffff 2 3 4 5 6 7 8 9 a 7*0 ffff
  //   contents of rom_2 (hex, n*v repeats v):
  //   10 20 30 40 50 60 70 80 90 a0
  //   contents of rom_3 (hex, n*v repeats v):
  //   1 2 3 4 5 6 7 8 9 a
endmodule
